# Fritzing sketch fritzingSketch (saved by Fritzing 0.9.3b)
breadboards: 1

parts:
  WeMos_D1_R1 = WeMos D1 R2
  Mod1 = KY-015 Temperature & Humidity Sensor Module [package="Breakout board"]
  Parça1 = MicroSD Card Module
  ZS-042_RTC1 = ZS-042 RTC Module
  LCM1602_IIC1 = LCM1602 IIC [part_number="LCM1602 IIC" chip_label="LCM1602 IIC" package="DIP (Dual Inline) [THT]"]
  LCD1 = LCD screen

nets:
  N1: WeMos_D1_R1.D2, Mod1.S
  N2: WeMos_D1_R1.D3, LCM1602_IIC1.SCL
  N3: WeMos_D1_R1.D4, LCM1602_IIC1.SDA
  N4: WeMos_D1_R1.D10, Parça1.CS
  N5: WeMos_D1_R1.D11, Parça1.MOSI
  N6: WeMos_D1_R1.D12, Parça1.MISO
  N7: WeMos_D1_R1.D13, Parça1.SCK
  N8: WeMos_D1_R1.D14, ZS-042_RTC1.SDA
  N9: WeMos_D1_R1.D15, ZS-042_RTC1.SCL
  GND: WeMos_D1_R1.GND, Mod1.-, Parça1.GND, ZS-042_RTC1.GND, LCM1602_IIC1.GND
  VCC: WeMos_D1_R1.5V, Mod1.Vin, Parça1.VCC, ZS-042_RTC1.VCC, LCM1602_IIC1.VCC
  VSS: LCM1602_IIC1.VSS, LCD1.VSS
  VDD: LCM1602_IIC1.VDD, LCD1.VDD
  N10: LCM1602_IIC1.V0, LCD1.V0
  N11: LCM1602_IIC1.RS, LCD1.RS
  N12: LCM1602_IIC1.RW, LCD1.R/W
  N13: LCM1602_IIC1.E, LCD1.E
  N14: LCM1602_IIC1.D0, LCD1.DB0
  N15: LCM1602_IIC1.D1, LCD1.DB1
  N16: LCM1602_IIC1.D2, LCD1.DB2
  N17: LCM1602_IIC1.D3, LCD1.DB3
  N18: LCM1602_IIC1.D4, LCD1.DB4
  N19: LCM1602_IIC1.D5, LCD1.DB5
  N20: LCM1602_IIC1.D6, LCD1.DB6
  N21: LCM1602_IIC1.D7, LCD1.DB7
  N22: LCM1602_IIC1.A, LCD1.LED+
  N23: LCM1602_IIC1.K, LCD1.LED-

custom parts:
  WeMos D1 R2: The D1 R2 is a mini wifi board based on the ESP-8266EX.
  KY-015 Temperature & Humidity Sensor Module: KY-015 temperature and humidity sensor module, provides a low-latency serial interface to measure humidity and temperature.
  LCM1602 IIC: I2C-Module to use a 1602 or 2004 LCD on with the wire.h libory Serial LCD Modul
